// Digital circuit ADD 6bit.dig as structural Verilog
module ADD_6bit (
  input  [5:0] A_5_0,
  input  Cin,
  input  [5:0] B_5_0,
  output [5:0] O_5_0,
  output Cout
);

  wire fa_1bit_2_cout, fa_1bit_3_cout, fa_1bit_4_cout, fa_1bit_5_cout, fa_1bit_6_cout;

  FA_1bit fa_1bit_1 (.X(A_5_0[5]), .Y(B_5_0[5]), .S(O_5_0[5]), .Cout(Cout), .Cin(fa_1bit_2_cout));
  FA_1bit fa_1bit_2 (.X(A_5_0[4]), .Y(B_5_0[4]), .S(O_5_0[4]), .Cout(fa_1bit_2_cout), .Cin(fa_1bit_3_cout));
  FA_1bit fa_1bit_3 (.X(A_5_0[3]), .Y(B_5_0[3]), .S(O_5_0[3]), .Cout(fa_1bit_3_cout), .Cin(fa_1bit_4_cout));
  FA_1bit fa_1bit_4 (.X(A_5_0[2]), .Y(B_5_0[2]), .S(O_5_0[2]), .Cout(fa_1bit_4_cout), .Cin(fa_1bit_5_cout));
  FA_1bit fa_1bit_5 (.X(A_5_0[1]), .Y(B_5_0[1]), .S(O_5_0[1]), .Cout(fa_1bit_5_cout), .Cin(fa_1bit_6_cout));
  FA_1bit fa_1bit_6 (.X(A_5_0[0]), .Y(B_5_0[0]), .S(O_5_0[0]), .Cout(fa_1bit_6_cout), .Cin(Cin));

  // Other names for the same wires on the sheet: A_0 = A_5_0[0]; A_1 = A_5_0[1]; A_2 = A_5_0[2]; A_3 = A_5_0[3];
  //   A_4 = A_5_0[4]; A_5 = A_5_0[5]; B_0 = B_5_0[0]; B_1 = B_5_0[1]; B_2 = B_5_0[2]; B_3 = B_5_0[3]; B_4 = B_5_0[4];
  //   B_5 = B_5_0[5]; O_0 = O_5_0[0]; O_1 = O_5_0[1]; O_2 = O_5_0[2]; O_3 = O_5_0[3]; O_4 = O_5_0[4]; O_5 = O_5_0[5]
endmodule
