// Digital circuit CPU 6bit.dig as structural Verilog
module CPU_6bit (
  input  [14:0] Wrd_14_0,
  input  CLK,
  input  WE,
  input  PC_EN,
  input  [2:0] Wr_2_0,
  output [14:0] RD2_14_0,
  output [5:0] R,
  output [2:0] reg1,
  output [2:0] reg2,
  output [5:0] reg1_value,
  output [1:0] op,
  output [5:0] Imm_value
);

  wire CPU_CLK, Imm_sel, jmp_sel, REG_EN, ZF;
  wire [1:0] XX;
  wire [2:0] multiplexer_1_out, pc_adder_3bit_1_o_2_0, program_counter_3bit_1_dout_2_0, value;
  wire [3:0] Opcode;
  wire [5:0] reg_set_6bit_1_b_5_0;

  Multiplexer #(.Bits(3)) multiplexer_1 (
    .sel(jmp_sel), .in_0(pc_adder_3bit_1_o_2_0), .in_1(reg1), .out(multiplexer_1_out));
  PC_Adder_3bit pc_adder_3bit_1 (.I_2_0(program_counter_3bit_1_dout_2_0), .O_2_0(pc_adder_3bit_1_o_2_0));
  Program_Counter_3bit program_counter_3bit_1 (
    .Din_2_0(multiplexer_1_out), .CLK(CPU_CLK), .Dout_2_0(program_counter_3bit_1_dout_2_0));
  and and_1 (CPU_CLK, PC_EN, CLK);
  SRAM___8x15 sram___8x15_1 (
    .RA1_2_0(program_counter_3bit_1_dout_2_0), .RA2_2_0(3'b000), .WA_2_0(Wr_2_0), .Wrd_14_0(Wrd_14_0),
    .WE(WE), .CLK(CLK), .RD1_14_0({Opcode, reg1, reg2, value, XX}), .RD2_14_0(RD2_14_0));
  reg_set_6bit reg_set_6bit_1 (
    .Wrd_5_0(R), .Wr_2_0(reg1), .WE(REG_EN), .CLK(CPU_CLK), .RA_2_0(reg1), .RB_2_0(reg2), .A_5_0(reg1_value),
    .B_5_0(reg_set_6bit_1_b_5_0));
  CU_6bit cu_6bit_1 (.Opcode_3_0(Opcode), .ZF(ZF), .Op_1_0(op), .REG_EN(REG_EN), .Imm_sel(Imm_sel), .JMP_sel(jmp_sel));
  // ALU_6bit alu_6bit_1: pin names not known; wires that end beside it: op, reg1_value, Imm_value, R, ZF
  Multiplexer #(.Bits(6)) multiplexer_2 (
    .sel(Imm_sel), .in_0(reg_set_6bit_1_b_5_0), .in_1({reg2, value}), .out(Imm_value));

  // Other names for the same wires on the sheet: value[5:3] = reg2; reg1_jmp_address[2:0] = reg1; A[5:0] = reg1_value;
  //   B[5:0] = Imm_value; RD2[14:0] = RD2_14_0; Wr[2:0] = Wr_2_0; Wrd[14:0] = Wrd_14_0
endmodule
