// Digital circuit NOT 6bit.dig as structural Verilog
module NOT_6bit (
  input  [5:0] X_5_0,
  output [5:0] Y_5_0
);

  not not_1 (Y_5_0[0], X_5_0[0]);
  not not_2 (Y_5_0[1], X_5_0[1]);
  not not_3 (Y_5_0[2], X_5_0[2]);
  not not_4 (Y_5_0[3], X_5_0[3]);
  not not_5 (Y_5_0[4], X_5_0[4]);
  not not_6 (Y_5_0[5], X_5_0[5]);
endmodule
