// Digital circuit Program Counter 3bit.dig as structural Verilog
module Program_Counter_3bit (
  input  CLK,
  input  [2:0] Din_2_0,
  output [2:0] Dout_2_0
);

  _1bit_reg _1bit_reg_1 (.Dout(Dout_2_0[0]), .Din(Din_2_0[0]), .Sel(1'b1), .CLK(CLK));
  _1bit_reg _1bit_reg_2 (.Dout(Dout_2_0[1]), .Din(Din_2_0[1]), .Sel(1'b1), .CLK(CLK));
  _1bit_reg _1bit_reg_3 (.Dout(Dout_2_0[2]), .Din(Din_2_0[2]), .Sel(1'b1), .CLK(CLK));

  // Other names for the same wires on the sheet: D_0 = Din_2_0[0]; D_1 = Din_2_0[1]; D_2 = Din_2_0[2];
  //   O_0 = Dout_2_0[0]; O_1 = Dout_2_0[1]; O_2 = Dout_2_0[2]
endmodule
