// Digital circuit reg 6bit.dig as structural Verilog
module reg_6bit (
  input  Sel,
  input  CLK,
  input  [5:0] Din_5_0,
  output [5:0] Dout_5_0
);

  _1bit_reg _1bit_reg_1 (.Dout(Dout_5_0[0]), .Din(Din_5_0[0]), .Sel(Sel), .CLK(CLK));
  _1bit_reg _1bit_reg_2 (.Dout(Dout_5_0[1]), .Din(Din_5_0[1]), .Sel(Sel), .CLK(CLK));
  _1bit_reg _1bit_reg_3 (.Dout(Dout_5_0[2]), .Din(Din_5_0[2]), .Sel(Sel), .CLK(CLK));
  _1bit_reg _1bit_reg_4 (.Dout(Dout_5_0[3]), .Din(Din_5_0[3]), .Sel(Sel), .CLK(CLK));
  _1bit_reg _1bit_reg_5 (.Dout(Dout_5_0[4]), .Din(Din_5_0[4]), .Sel(Sel), .CLK(CLK));
  _1bit_reg _1bit_reg_6 (.Dout(Dout_5_0[5]), .Din(Din_5_0[5]), .Sel(Sel), .CLK(CLK));

  // Other names for the same wires on the sheet: D_0 = Din_5_0[0]; D_1 = Din_5_0[1]; D_2 = Din_5_0[2];
  //   D_3 = Din_5_0[3]; D_4 = Din_5_0[4]; D_5 = Din_5_0[5]; O_0 = Dout_5_0[0]; O_1 = Dout_5_0[1]; O_2 = Dout_5_0[2];
  //   O_3 = Dout_5_0[3]; O_4 = Dout_5_0[4]; O_5 = Dout_5_0[5]
endmodule
